# Fritzing sketch wiringguide (saved by Fritzing 0.9.3b)
breadboards: 1

parts:
  Mega_2560 = Arduino Mega 2560 (Rev3)
  female_RJ45_Team_A = RJ45 Jack [package=rj45-8]
  C1 = Ceramic Capacitor [capacitance=100nF package="100 mil [THT, multilayer]"]
  male_RJ45_Team_A = RJ45 Jack [package=rj45-8]
  A1 = Square Pushbutton
  A2 = Square Pushbutton
  A3 = Square Pushbutton
  A4 = Square Pushbutton
  part = LCD screen
  R1 = Resistor [tolerance=±5% resistance=2.2k package=THT]

nets:
  N1: Mega_2560.GND, female_RJ45_Team_A.2, C1.0, part.R/W, R1.Pin_1
  5V: Mega_2560.5V, part.VDD, part.LED+
  N2: Mega_2560.D30, female_RJ45_Team_A.1, C1.1
  N3: Mega_2560.D42, part.DB7
  N4: Mega_2560.D43, part.DB6
  N5: Mega_2560.D44, part.DB5
  N6: Mega_2560.D45, part.DB4
  N7: Mega_2560.D46, part.DB3
  N8: Mega_2560.D47, part.DB2
  N9: Mega_2560.D48, part.DB1
  N10: Mega_2560.D49, part.DB0
  N11: Mega_2560.D50, part.E
  N12: Mega_2560.D51, part.RS
  N13: male_RJ45_Team_A.1, A1.leg1
  N14: male_RJ45_Team_A.2, A1.leg0
  N15: male_RJ45_Team_A.3, A2.leg1
  N16: male_RJ45_Team_A.4, A2.leg0
  N17: male_RJ45_Team_A.5, A3.leg1
  N18: male_RJ45_Team_A.6, A3.leg0
  N19: male_RJ45_Team_A.7, A4.leg1
  N20: male_RJ45_Team_A.8, A4.leg0
  N21: part.VSS, part.LED-
  N22: part.V0, R1.Pin_0

notes:
  Team A female RJ45:
  RJ45 1,3,5,7 to D30,D31,D32,D33
  RJ45 2,4,6,8 to GND
  Team B female RJ45:
  RJ45 1,3,5,7 to D34,D35,D36,D37
  RJ45 2,4,6,8 to GND
  Team C female RJ45
  RJ45 1,3,5,7 to D38,D39,D40,D41
  RJ45 2,4,6,8 to GND
  100nF capacitors
  between 1 and 2, 3 and 4, 5 and 6, and 7 and 8 on all female RJ45s
  repeat for teams B and C
  need 220R
  resistor between LED+ and 5V if screen doesn't supply
  TODO:
  clear and mode switches
